# Fritzing sketch apds-9960 (saved by Fritzing 0.9.3b)

parts:
  PART1 = APDS-9960 RGB and Gesture Sensor [part_number=SEN-12787]
  Part9 = Tessel 2

nets:
  VCC: PART1.VCC, Part9.3V3
  GND: PART1.GND, Part9.GND
  N1: PART1.SDA, Part9.1
  N2: PART1.SCL, Part9.0
  N3: PART1.INT, Part9.2

custom parts:
  APDS-9960 RGB and Gesture Sensor: Breakout board for the Avago APDS-9960 proximity, light, RGB, and gesture sensors. Please visit www.sparkfun.com to learn more.
  Tessel 2: Draft version of Tessel 2
